# Fritzing sketch Sepatu (saved by Fritzing 0.9.2b)

parts:
  R1 = Resistor [tolerance=±5% resistance=1k package=THT]  # not connected
  Part1 = Arduino Mega 2560 (Rev3)
  R2 = Photocell (LDR) [package=THT]  # not connected
  Mod1 = KY-008 Laser Transmitter Module [package="Breakout board"]  # not connected
  R3 = Resistor [tolerance=±5% resistance=1k package=THT]
  R4 = Photocell (LDR) [package=THT]
  Mod2 = KY-008 Laser Transmitter Module [package="Breakout board"]  # not connected
  R5 = Resistor [tolerance=±5% resistance=1k package=THT]
  R6 = Photocell (LDR) [package=THT]
  Mod3 = KY-008 Laser Transmitter Module [package="Breakout board"]  # not connected
  R7 = Resistor [tolerance=±5% resistance=1k package=THT]  # not connected
  R8 = Photocell (LDR) [package=THT]  # not connected
  Mod4 = KY-008 Laser Transmitter Module [package="Breakout board"]  # not connected
  R9 = Resistor [tolerance=±5% resistance=1k package=THT]
  R10 = Photocell (LDR) [package=THT]
  Mod5 = KY-008 Laser Transmitter Module [package="Breakout board"]  # not connected
  R15 = Resistor [tolerance=±5% resistance=1k package=THT]
  R16 = Photocell (LDR) [package=THT]
  R17 = Photocell (LDR) [package=THT]
  R18 = Photocell (LDR) [package=THT]
  R19 = Photocell (LDR) [package=THT]
  R20 = Photocell (LDR) [package=THT]
  Mod6 = KY-008 Laser Transmitter Module [package="Breakout board"]  # not connected
  Mod7 = KY-008 Laser Transmitter Module [package="Breakout board"]  # not connected
  Mod8 = KY-008 Laser Transmitter Module [package="Breakout board"]  # not connected
  Mod9 = KY-008 Laser Transmitter Module [package="Breakout board"]
  Mod10 = KY-008 Laser Transmitter Module [package="Breakout board"]
  R21 = Resistor [tolerance=±5% resistance=1k package=THT]
  R23 = Resistor [tolerance=±5% resistance=1k package=THT]
  R24 = Resistor [tolerance=±5% resistance=1k package=THT]
  R25 = Resistor [tolerance=±5% resistance=1k package=THT]
  Part4 = SRF05 Ultrasonic Rangefinder
  WeMos_D1_Mini1 = WeMos D1 Mini

nets:
  N1: Part1.A8, R5.Pin_1, R6.pin_1
  N2: Part1.A9, R3.Pin_1, R4.pin_1
  N3: Part1.A11, R9.Pin_1, R10.pin_1
  N4: Part1.A14, R20.pin_0, R24.Pin_1
  N5: Part1.A15, R17.pin_0, R23.Pin_1
  N6: Part1.A5, R15.Pin_0, R19.pin_0
  N7: Part1.A6, R16.pin_0, R21.Pin_0, R21.Pin_1
  N8: Part1.A7, R18.pin_0, R25.Pin_1
  GND: Part1.GND, Mod10.-, R24.Pin_0, Part4.GND, WeMos_D1_Mini1.G
  N9: Part1.3V3, Mod10.S
  N10: Part1.5V, R16.pin_1, R19.pin_1, R20.pin_1
  N11: Part1.D0_RX0, WeMos_D1_Mini1.TX
  N12: Part1.D1_TX0, WeMos_D1_Mini1.RX
  N13: Part1.D2_PWM, Part4.Echo
  N14: Part1.D3_PWM, Part4.Trig
  N15: Mod9.S, Mod9.NC

custom parts:
  KY-008 Laser Transmitter Module: KY-008 Laser Transmitter Module, emits a dot shaped red laser beam.
  WeMos D1 Mini: The D1 mini is a mini wifi board based on ESP-8266EX.
