# Fritzing sketch Sawah (saved by Fritzing 0.9.2b)

parts:
  Part1 = Arduino Uno (Rev3) - ICSP
  KY-1 = Keyes Relay [package=THT]
  KY-2 = Keyes Relay [package=THT]
  부품3 = FC-28 Soil Hygrometer Module - Probe
  부품4 = FC-28 Soil Hygrometer Module
  e-radionica_com4 = LM393 LDR breakout [part_number=100027]
  WATER_PUMP3 = water pump/motor  # not connected
  BULB1 = Incandescent light bulb small [package="bulb sm"]
  Power_plug1 = Power plug  # not connected
  Solar_Cell = Solar Cell
  U1 = LIPO-1000mAh [package=lipo-1000]
  Solar_Cell_Controller1 = Power Cell LiPo Charger/Booster
  U2 = LCD-16X2 [package=lcd-16x2]
  LCM1602_IIC1 = LCM1602 IIC [part_number="LCM1602 IIC" chip_label="LCM1602 IIC" package="DIP (Dual Inline) [THT]"]

nets:
  N1: Part1.A0, 부품4.AO
  N2: Part1.A1, e-radionica_com4.DO
  N3: Part1.A4/SDA, LCM1602_IIC1.SDA
  N4: Part1.A5/SCL, LCM1602_IIC1.SCL
  N5: Part1.D8, KY-1.signal
  GND: Part1.GND, KY-1.ground, 부품4.GND, e-radionica_com4.GND, LCM1602_IIC1.GND
  N6: Part1.D7, KY-2.signal
  VCC: Part1.5V, KY-1.power, 부품4.VCC, LCM1602_IIC1.VCC
  N7: KY-1.NC, BULB1.1
  N8: KY-1.C, BULB1.2
  N9: KY-1.NO, U1.+, Solar_Cell_Controller1.VCC
  N10: KY-2.NC, U1.-
  N11: 부품3.POS, 부품4.POS
  N12: 부품3.NEG, 부품4.NEG
  N13: Solar_Cell.+, Solar_Cell_Controller1.5VIN
  N14: Solar_Cell.-, Solar_Cell_Controller1.GND
  VSS: U2.VSS, LCM1602_IIC1.VSS
  VDD: U2.VDD, LCM1602_IIC1.VDD
  N15: U2.VO, LCM1602_IIC1.V0
  N16: U2.RS, LCM1602_IIC1.RS
  N17: U2.R_W, LCM1602_IIC1.RW
  N18: U2.E, LCM1602_IIC1.E
  N19: U2.DB0, LCM1602_IIC1.D0
  N20: U2.DB1, LCM1602_IIC1.D1
  N21: U2.DB2, LCM1602_IIC1.D2
  N22: U2.DB3, LCM1602_IIC1.D3
  N23: U2.DB4, LCM1602_IIC1.D4
  N24: U2.DB5, LCM1602_IIC1.D5
  N25: U2.DB6, LCM1602_IIC1.D6
  N26: U2.DB7, LCM1602_IIC1.D7
  N27: U2.A, LCM1602_IIC1.A
  N28: U2.K, LCM1602_IIC1.K
  N29: LCM1602_IIC1.LED_A, LCM1602_IIC1.LED_B

notes:
  Baterai
  Lampu
  Sensor LDR
  Sensor Soil Moisture
  Water Pump Mini
  Relay 2 Channel
  Arduino Uno R3
  Solar Panel
  Solar Cell Controller
  LCD 16x2 I2C

custom parts:
  Keyes Relay: The Keyes 5V relay module is suitable for SCM development, home appliance control. It uses a 5V~12V TIL control signal which can control DC / AC signal.
  FC-28 Soil Hygrometer Module - Probe: The FC-28 is a soil hygrometer module that uses the Texas Instruments LM393 comparator chip to provide an analog measurement of soil humidity.
  FC-28 Soil Hygrometer Module: The FC-28 is a soil hygrometer module that uses the Texas Instruments LM393 comparator chip to provide an analog measurement of soil humidity. The digital output is high when soil moisture is over a certain threshold, as determined by adjusting the potentiometer.
  water pump/motor: WATER PUMP BY ARDUBLOCKTR
  LCM1602 IIC: I2C-Module to use a 1602 or 2004 LCD on with the wire.h libory Serial LCD Modul
